# Fritzing sketch NHPT (saved by Fritzing 0.9.3b)

parts:
  Part1 = Arduino Mega ADK (Rev3)
  R1 = Resistor [tolerance=±5% resistance=3.3k package=THT]
  Part2 = Analog Digital MUX Breakout
  R2 = Resistor [tolerance=±5% resistance=3.3k package=THT]
  R3 = Resistor [tolerance=±5% resistance=3.3k package=THT]
  R4 = Resistor [tolerance=±5% resistance=3.3k package=THT]
  R5 = Resistor [tolerance=±5% resistance=3.3k package=THT]
  U1 = AVR 10-pin ICSP Header [package=2x5-shrouded_smd]
  R24 = Resistor [tolerance=±5% resistance=3.3k package=THT]
  R30 = Resistor [tolerance=±5% resistance=3.3k package=THT]
  R31 = Resistor [tolerance=±5% resistance=3.3k package=THT]
  R32 = Resistor [tolerance=±5% resistance=3.3k package=THT]
  R33 = Resistor [tolerance=±5% resistance=3.3k package=THT]
  R34 = Resistor [tolerance=±5% resistance=3.3k package=THT]
  R35 = Resistor [tolerance=±5% resistance=3.3k package=THT]
  R36 = Resistor [tolerance=±5% resistance=3.3k package=THT]
  R37 = Resistor [tolerance=±5% resistance=3.3k package=THT]
  R38 = Resistor [tolerance=±5% resistance=3.3k package=THT]
  R39 = Resistor [tolerance=±5% resistance=3.3k package=THT]
  U2 = AVR 10-pin ICSP Header [package=2x5-shrouded_smd]
  U3 = AVR 10-pin ICSP Header [package=2x5-shrouded_smd]
  U4 = AVR 10-pin ICSP Header [package=2x5-shrouded_smd]
  P1 = S1133 Si Photodiode [package="8mm Ceramic [THT]"]
  U5 = AVR 10-pin ICSP Header [package=2x5-shrouded_smd]
  U6 = AVR 10-pin ICSP Header [package=2x5-shrouded_smd]
  U7 = AVR 10-pin ICSP Header [package=2x5-shrouded_smd]
  U8 = AVR 10-pin ICSP Header [package=2x5-shrouded_smd]
  R40 = Resistor [tolerance=±5% resistance=330 package=THT]
  D1 = LTE-302 [package=lte-302]
  J1 = double row rounded female pin header, 30 pins [form="♀ (female rounded)"]

nets:
  N1: Part1.A8, R32.Pin_1, U2.4
  N2: Part1.A9, R33.Pin_1, U2.2
  N3: Part1.A10, R34.Pin_1, U3.10
  N4: Part1.A11, R35.Pin_1, U3.8
  N5: Part1.A12, R36.Pin_1, U3.6
  N6: Part1.A13, R37.Pin_1, U3.4
  N7: Part1.A14, R38.Pin_1, U3.2
  N8: Part1.A15, Part2.SIG, R39.Pin_1
  N9: Part1.A0, R1.Pin_1, U1.10
  N10: Part1.A1, R2.Pin_1, U1.8
  N11: Part1.A2, R3.Pin_1, U1.6
  N12: Part1.A3, R4.Pin_1, U1.4
  N13: Part1.A4, R5.Pin_1, U1.2
  N14: Part1.A5, R24.Pin_1, U2.10
  N15: Part1.A6, R30.Pin_1, U2.8
  N16: Part1.A7, R31.Pin_1, U2.6
  N17: Part1.D21/SCL, R36.Pin_0
  N18: Part1.D20/SDA, R35.Pin_0
  N19: Part1.D19/RX1, R34.Pin_0
  N20: Part1.D18/TX1, R33.Pin_0
  N21: Part1.D17/RX2, R32.Pin_0
  N22: Part1.D16/TX2, R31.Pin_0
  N23: Part1.D15/RX3, R30.Pin_0
  N24: Part1.D14/TX3, R24.Pin_0
  5V: Part1.5V, Part2.VCC
  N25: Part1.GND, J1.pin1
  N26: Part1.D3_PWM, R5.Pin_0
  N27: Part1.D4_PWM, R4.Pin_0
  N28: Part1.D5_PWM, R3.Pin_0
  N29: Part1.D6_PWM, R2.Pin_0
  N30: Part1.D7_PWM, R1.Pin_0
  N31: Part1.D25, U6.9
  N32: Part1.D27, U6.1
  N33: Part1.D29, U5.3
  N34: Part1.D31, U7.5
  N35: Part1.D33, U8.7
  N36: Part1.D35, D1.A
  N37: Part1.D36, R37.Pin_0
  N38: Part1.D37, Part2.S0
  N39: Part1.D38, R38.Pin_0
  N40: Part1.D39, Part2.S1
  N41: Part1.D40, R39.Pin_0
  N42: Part1.D41, Part2.S2
  N43: Part1.D43, Part2.S3
  N44: Part2.C0, U4.10
  N45: Part2.C1, U4.8
  N46: Part2.C2, U4.6
  N47: Part2.C3, U4.4
  N48: Part2.C4, U4.2
  N49: Part2.C5, P1.cathode
  N50: Part2.GND, J1.pin24
  N51: Part2.EN, J1.pin25
  N52: U1.1, J1.pin6
  N53: U1.3, J1.pin5
  N54: U1.5, J1.pin4
  N55: U1.7, J1.pin3
  N56: U1.9, J1.pin2
  N57: U2.1, J1.pin11
  N58: U2.3, J1.pin10
  N59: U2.5, J1.pin9
  N60: U2.7, J1.pin8
  N61: U2.9, J1.pin7
  N62: U3.1, J1.pin16
  N63: U3.3, J1.pin15
  N64: U3.5, J1.pin14
  N65: U3.7, J1.pin13
  N66: U3.9, J1.pin12
  N67: U4.1, J1.pin26
  N68: U4.3, J1.pin27
  N69: U4.5, J1.pin28
  N70: U4.7, J1.pin29
  N71: U4.9, J1.pin30
  N72: P1.anode, J1.pin17
  N73: U5.1, U5.4
  N74: U5.2, U7.9
  N75: U5.5, U5.8
  N76: U5.6, J1.pin23
  N77: U5.7, U5.10
  N78: U5.9, U6.2
  N79: U6.3, U6.6
  N80: U6.4, J1.pin22
  N81: U6.5, U6.8
  N82: U6.7, U6.10
  N83: U7.1, U7.4
  N84: U7.2, U8.9
  N85: U7.3, U7.6
  N86: U7.7, U7.10
  N87: U7.8, J1.pin21
  N88: U8.1, U8.4
  N89: U8.2, J1.pin19
  N90: U8.3, U8.6
  N91: U8.5, U8.8
  N92: U8.10, J1.pin20
  N93: R40.Pin_0, J1.pin18
  N94: R40.Pin_1, D1.C

notes:
  Common ground
  LED shrouded header 1
  (LEDs 1-5)
  LED shrouded header 2
  (LEDs 6-10)
  LED shrouded header 3 (LEDs 11-15)
  LED shrouded header 4 (LEDs 16-20)
  LED 21
  diode shrouded header 1
  (diodes 1-5)
  diode shrouded header 4
  (diodes 16-20)
  For the LEDS: Each up-down pair should be connected to a single LED (so each "box" is connected to 5 LEDs). The numbers go from right to left (i.e. most right is LED #1). The LEDs are turned on in sets of 4. As each set gets 5V and they are connected in serial, each LED gets ~1.25V (which matches the specification of 1.2-1.3V)
  diode shrouded header 2
  (diodes 6-10)
  diode shrouded header 3
  (diodes 11-15)
